# Fritzing sketch circuito (saved by Fritzing 1.0.0d)

parts:
  Driver1 = 28BYJ-48 Driver Module [part_number=ULN2003 package=THT]
  SM1 = 28BYJ-48 Stepper Motor [part_number=28BYJ-48]  # not connected
  C1 = Electrolytic Capacitor [capacitance=1µF voltage=35V package="100 mil [THT, electrolytic]"]  # not connected
  J1 = Basic Servo
  SM2 = 28BYJ-48 Stepper Motor [part_number=28BYJ-48]  # not connected
  Driver2 = 28BYJ-48 Driver Module [part_number=ULN2003 package=THT]
  J2 = Power Jack [package=power_jack_pth]
  M1 = DOIT Esp32 DevKit v1 (30 pins long, 11 pins width) [part_number=ESP32S-PIN30]
  microSD1 = MicroSD Card Module
  C2 = Electrolytic Capacitor [capacitance=1µF voltage=35V package="100 mil [THT, electrolytic]"]  # not connected
  C3 = Electrolytic Capacitor [capacitance=1µF voltage=35V package="100 mil [THT, electrolytic]"]  # not connected
  J3 = Piezo Speaker  # not connected
  S1 = Pushbutton [package="[THT]"]
  S2 = Pushbutton [package="[THT]"]
  R2 = Resistor [tolerance=±5% power=0.25W resistance=220 package=THT]  # not connected
  R3 = Resistor [tolerance=±5% power=0.25W resistance=220 package=THT]

nets:
  N1: Driver1.IN1, M1.D26
  N2: Driver1.IN2, M1.D25
  N3: Driver1.IN3, M1.D33
  N4: Driver1.IN4, M1.D32
  GND: Driver1.GND, Driver2.GND
  N5: Driver1.Vmotor, Driver2.Vmotor
  N6: J1.pulse, M1.D15
  N7: Driver2.IN1, M1.D13
  N8: Driver2.IN2, M1.D12
  N9: Driver2.IN3, M1.D14
  N10: Driver2.IN4, M1.D27
  GND_2: J2.GND, M1.GND
  N11: J2.GNDBREAK, M1.VIN
  3V3: M1.3V3, microSD1.VCC
  N12: M1.D5, microSD1.CS
  N13: M1.D18, microSD1.SCK
  N14: M1.D19, microSD1.MISO
  N15: M1.D23, microSD1.MOSI
  N16: M1.D34, S2.Pin_3, S2.Pin_4
  N17: S1.Pin_1, S1.Pin_2, R3.Pin_0

custom parts:
  28BYJ-48 Driver Module: Generic male header
  28BYJ-48 Stepper Motor: Unipolar Stepper Motor 28BYJ-48 Top coil - pink & orange Bottom coil - blue & yellow Common rail - red Connector pins: blue - pink - yellow - orange - red
  DOIT Esp32 DevKit v1 (30 pins long, 11 pins width): The DOIT Esp32 DevKit v1 is one of the development board created by DOIT to evaluate the ESP-WROOM-32 module. It is based on the ESP32 microcontroller that boasts Wifi, Bluetooth, Ethernet and Low Power support all in a single chip. (vanepp) made breadboard work, adjusted pin numbering and labels and reduced size of schematic and cleaned up pcb. This chip is 30pins long (2 x15) and 11 pins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
