# Fritzing sketch circuito_pb (saved by Fritzing 0.9.10b)
stripboards: 1

parts:
  SM4 = 28BYJ-48 Stepper Motor [part_number=28BYJ-48]  # not connected
  M10 = DOIT Esp32 DevKit v1 (30 pins long, 11 pins width) [part_number=ESP32S-PIN30]
  J43 = female pin header, 2 pins [form="♀ (female)"]
  Driver1 = 28BYJ-48 Driver Module [part_number=ULN2003 package=THT]  # not connected
  J44 = Power Jack [package=power_jack_smd]
  C1 = Capacitor Polarized [package=panasonic_c]
  J45 = Basic Servo  # not connected

nets:
  N1: M10.GND, M10.RX0, M10.D34, J44.GNDBREAK, C1.-
  N2: M10.D15, M10.D13
  N3: M10.D2, M10.D12
  N4: M10.D4, M10.RX2, M10.TX2, M10.D26, M10.D27, M10.D14
  N5: M10.D5, M10.D22, M10.VP, M10.D25
  N6: M10.D18, M10.D19, M10.D32, M10.D33
  N7: M10.D21, M10.D35
  N8: M10.TX0, M10.D23, M10.EN, M10.VN
  VIN: M10.VIN, J43.pin1, J43.pin2, J44.GND

notes:
  mi   scl  v+  gr mo cs

custom parts:
  28BYJ-48 Stepper Motor: Unipolar Stepper Motor 28BYJ-48 Top coil - pink & orange Bottom coil - blue & yellow Common rail - red Connector pins: blue - pink - yellow - orange - red
  DOIT Esp32 DevKit v1 (30 pins long, 11 pins width): The DOIT Esp32 DevKit v1 is one of the development board created by DOIT to evaluate the ESP-WROOM-32 module. It is based on the ESP32 microcontroller that boasts Wifi, Bluetooth, Ethernet and Low Power support all in a single chip. (vanepp) made breadboard work, adjusted pin numbering and labels and reduced size of schematic and cleaned up pcb. This chip is 30pins long (2 x15) and 11 pins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
  28BYJ-48 Driver Module: Generic male header
